# Fritzing sketch ESP32-HX711-MQTT (saved by Fritzing 0.9.3b)

parts:
  Wire = Header 4 [package=screwterminal-3.5mm-4_lock]
  U1 = ESP32S-HiLetgo [part_number=ESP32S-HiLetgo]
  S1 = Momentary Switch [package=tactile_switch_smd]
  PART1 = SparkFun Load Cell Amplifier - HX711 [part_number=HX711]
  piezo_speaker = Piezo Speaker

nets:
  N1: Wire.1, PART1.GRN
  N2: Wire.2, PART1.WHT
  N3: Wire.3, PART1.BLK
  N4: Wire.4, PART1.RED
  3.3V: U1.3.3, PART1.VCC
  N5: U1.GPIO25, PART1.CLK
  N6: U1.GPIO26, PART1.DAT
  N7: U1.GPIO12, piezo_speaker.pin2
  GND: U1.GND, S1.3, PART1.GND, piezo_speaker.pin1
  N8: U1.GPIO0, S1.1, S1.2

notes:
  TANITA
  LOAD CELL
  wake up button
  Load cells of the original weight scale.
  Connection is my guess work by measureing resistance between wires.
  push button in the weight scale is
  re-used.

custom parts:
  ESP32S-HiLetgo: HiLetgo ESP-WROOM-32 ESP32 ESP-32S Development Board 2.4GHz Dual-Mode WiFi + Bluetooth Dual Cores Microcontroller The ESP32 integrated with Antenna switches, RF Balun, power amplifiers, low-noise amplifiers, filters, and management modules, and the entire solution occupies the least area of PCB. 2.4 GHz Wi-Fi plus Bluetooth dual-mode chip, with TSMC Ultra-low power consumption 40nm technology,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
  SparkFun Load Cell Amplifier - HX711: The SparkFun Load Cell Amplifier is a small breakout board for the HX711 IC that allows you to easily read load cells to measure weight. By connecting the amplifier to your microcontroller you will be able to read the changes in the resistance of the load cell and with some calibration you’ll be able to get very accurate weight measurements. This can be handy for creating your own industrial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
